# Fritzing sketch MatrixSenderCircuit (saved by Fritzing 0.9.2b)
breadboards: 1

parts:
  S123 = female pin header, 6 pins [form="♀ (female)"]
  S456 = female pin header, 6 pins [form="♀ (female)"]
  S789 = female pin header, 6 pins [form="♀ (female)"]
  D1 = male pin header, 1 pin [form="♂ (male)"]
  D3 = male pin header, 1 pin [form="♂ (male)"]
  D2 = male pin header, 1 pin [form="♂ (male)"]
  D6 = Rectifier Diode [part_number=1N4001 package="Melf DO-213 AB [SMD]"]
  D7 = Rectifier Diode [part_number=1N4001 package="Melf DO-213 AB [SMD]"]
  D8 = Rectifier Diode [part_number=1N4001 package="Melf DO-213 AB [SMD]"]
  D9 = Rectifier Diode [part_number=1N4001 package="Melf DO-213 AB [SMD]"]
  D10 = Rectifier Diode [part_number=1N4001 package="Melf DO-213 AB [SMD]"]
  D11 = Rectifier Diode [part_number=1N4001 package="Melf DO-213 AB [SMD]"]
  D12 = Rectifier Diode [part_number=1N4001 package="Melf DO-213 AB [SMD]"]
  D13 = Rectifier Diode [part_number=1N4001 package="Melf DO-213 AB [SMD]"]
  D14 = Rectifier Diode [part_number=1N4001 package="Melf DO-213 AB [SMD]"]
  A3 = male pin header, 1 pin [form="♂ (male)"]
  A2 = male pin header, 1 pin [form="♂ (male)"]
  A1 = male pin header, 1 pin [form="♂ (male)"]
  Vcc = male pin header, 1 pin [form="♂ (male)"]
  R1 = Resistor [tolerance=±5% resistance=1k package=THT]
  R2 = Resistor [tolerance=±5% resistance=1k package=THT]
  R3 = Resistor [tolerance=±5% resistance=1k package=THT]

nets:
  N1: S123.pin1, D14.anode
  N2: S123.pin2, S456.pin2, S789.pin2, A1.pin1, R1.Pin_0
  N3: S123.pin3, D11.anode
  N4: S123.pin4, S456.pin4, S789.pin4, A2.pin1, R2.Pin_0
  N5: S123.pin5, D6.anode
  N6: S123.pin6, S456.pin6, S789.pin6, A3.pin1, R3.Pin_0
  N7: S456.pin1, D13.anode
  N8: S456.pin3, D10.anode
  N9: S456.pin5, D7.anode
  N10: S789.pin1, D12.anode
  N11: S789.pin3, D9.anode
  N12: S789.pin5, D8.anode
  N13: D1.pin1, D6.cathode, D11.cathode, D14.cathode
  N14: D3.pin1, D8.cathode, D9.cathode, D12.cathode
  N15: D2.pin1, D7.cathode, D10.cathode, D13.cathode
  N16: Vcc.pin1, R1.Pin_1, R2.Pin_1, R3.Pin_1
